// Logisim project control-logic.circ as structural Verilog: 1 circuit, main circuit control_logic
module control_logic (
  input  [31:0] Instruction,
  input  BrEq,
  input  BrLt,
  output PCSel,
  output RegWEn,
  output [2:0] ImmSel,
  output BrUn,
  output ASel,
  output BSel,
  output [3:0] ALUSel,
  output MemWEn,
  output [1:0] WBSel
);

  wire and_2_out, and_3_out, and_4_out, and_5_out, and_6_out, and_12_out, and_14_out, and_16_out, and_18_out,
       and_30_out, and_31_out, and_37_out, and_38_out, and_39_out, and_46_out, and_52_out, and_57_out,
       and_58_out, and_59_out, and_60_out, and_62_out, funct3_01_00, funct3_01_01, funct3_01_10,
       funct3_01_11, funct3_2_0, funct3_2_1, funct7_01_00, funct7_01_01, funct7_45_00, funct7_45_01, is_add,
       is_addi, is_and, is_andi, is_auipc, is_beq, is_bge, is_bgeu, is_blt, is_bltu, is_bne, is_Btype,
       is_Itype, is_jal, is_jalr, is_lb, is_lh, is_load, is_lui, is_lw, is_mul, is_mulh, is_mulhu, is_or,
       is_ori, is_Rtype, is_sb, is_sh, is_sll, is_slli, is_slt, is_slti, is_sra, is_srai, is_srl, is_srli,
       is_Stype, is_sub, is_sw, is_xor, is_xori, Itype_funct3_101, not_1_out, not_2_out, not_3_out,
       not_4_out, not_5_out, not_6_out, not_7_out, not_8_out, not_9_out, not_10_out, not_11_out, not_12_out,
       not_13_out, not_14_out, not_15_out, not_16_out, not_17_out, opcode_6_0, opcode_6_1, opcode_23_00,
       opcode_23_01, opcode_45_00, opcode_45_01, opcode_45_10, opcode_45_11, or_1_out, or_2_out, or_3_out,
       or_4_out, or_5_out, or_7_out, Rtype_funct3_000, Rtype_funct3_000_0, Rtype_funct3_001, Rtype_funct3_101;
  wire [5:0] priority_encoder_1_out;
  wire [15:14] rom_1_data;

  and and_1 (is_Rtype, opcode_23_00, opcode_45_11);
  and and_2 (and_2_out, opcode_23_01, opcode_45_11);
  and and_3 (and_3_out, is_Rtype, funct3_01_00);
  and and_4 (and_4_out, is_Rtype, funct3_01_11);
  and and_5 (and_5_out, is_Rtype, funct3_01_01);
  and and_6 (and_6_out, is_Btype, funct3_01_00);
  and and_7 (is_lui, and_2_out, opcode_6_0);
  and and_8 (Rtype_funct3_000, and_3_out, funct3_2_0);
  not not_1 (not_1_out, funct3_2_0);
  and and_9 (is_and, and_4_out, funct3_2_1);
  not not_2 (not_2_out, funct3_2_1);
  and and_10 (Rtype_funct3_101, and_5_out, funct3_2_1);
  not not_3 (not_3_out, funct3_2_1);
  and and_11 (is_beq, and_6_out, funct3_2_0);
  not not_4 (not_4_out, funct3_2_0);
  and and_12 (and_12_out, is_Btype, funct3_01_01);
  and and_13 (is_bne, and_12_out, funct3_2_0);
  not not_5 (not_5_out, funct3_2_0);
  and and_14 (and_14_out, is_Itype, funct3_01_00);
  and and_15 (is_addi, and_14_out, funct3_2_0);
  not not_6 (not_6_out, funct3_2_0);
  and and_16 (and_16_out, is_Itype, funct3_01_10);
  and and_17 (is_slti, and_16_out, funct3_2_0);
  not not_7 (not_7_out, funct3_2_0);
  and and_18 (and_18_out, is_Itype, funct3_01_01);
  and and_19 (is_slli, and_18_out, funct3_2_0);
  not not_8 (not_8_out, funct3_2_0);
  and and_20 (is_sb, is_Stype, funct3_01_00);
  and and_21 (is_lb, is_load, funct3_01_00);
  Comparator #(.width(2)) comparator_1 (
    .a(Instruction[3:2]), .b(2'b11), .gt(is_jal), .eq(opcode_23_01), .lt(opcode_23_00));
  Comparator #(.width(2)) comparator_2 (
    .a(Instruction[5:4]), .b(2'b10), .gt(opcode_45_11), .eq(opcode_45_10));  // open: lt
  Comparator #(.width(2)) comparator_3 (
    .a(Instruction[5:4]), .b(2'b01), .eq(opcode_45_01), .lt(opcode_45_00));  // open: gt
  Comparator #(.width(1)) comparator_4 (.a(Instruction[6]), .b(1'b1), .eq(opcode_6_1), .lt(opcode_6_0));  // open: gt
  and and_22 (is_xor, and_3_out, not_1_out);
  and and_23 (is_mulhu, and_4_out, not_2_out);
  and and_24 (Rtype_funct3_001, and_5_out, not_3_out);
  and and_25 (is_blt, and_6_out, not_4_out);
  and and_26 (is_bge, and_12_out, not_5_out);
  and and_27 (is_xori, and_14_out, not_6_out);
  and and_28 (is_ori, and_16_out, not_7_out);
  and and_29 (Itype_funct3_101, and_18_out, not_8_out);
  and and_30 (and_30_out, opcode_23_00, opcode_45_10);
  and and_31 (and_31_out, opcode_23_01, opcode_45_01);
  Priority_Encoder #(.select_enc(6)) priority_encoder_1 (
    .in0(is_add), .in1(is_mul), .in2(is_sub), .in3(is_sll), .in4(is_mulh), .in5(is_mulhu), .in6(is_slt),
    .in7(is_xor), .in8(is_srl), .in9(is_sra), .in10(is_or), .in11(is_and), .in12(is_lb), .in13(is_lh),
    .in14(is_lw), .in15(is_addi), .in16(is_slli), .in17(is_slti), .in18(is_xori), .in19(is_srli),
    .in20(is_srai), .in21(is_ori), .in22(is_andi), .in23(is_sb), .in24(is_sh), .in25(is_sw), .in26(is_beq),
    .in27(is_bne), .in28(is_blt), .in29(is_bge), .in30(is_bltu), .in31(is_bgeu), .in32(is_auipc),
    .in33(is_lui), .in34(is_jal), .in35(is_jalr), .out(priority_encoder_1_out));  // open: in36, in37, in38, in39, in40, in41, in42, in43, in44, in45, in46, in47, in48, in49, in50, in51, in52, in53, in54, in55, in56, in57, in58, in59, in60, in61, in62, in63, gs, en_out, en_in
  and and_32 (is_auipc, and_31_out, opcode_6_0);
  and and_33 (is_sh, is_Stype, funct3_01_01);
  and and_34 (is_lh, is_load, funct3_01_01);
  ROM #(.addrWidth(6), .dataWidth(16)) rom_1 (
    .addr(priority_encoder_1_out),
    .data({rom_1_data, WBSel, MemWEn, ALUSel, BSel, ASel, BrUn, ImmSel, RegWEn}));
  and and_35 (is_Stype, and_30_out, opcode_6_0);
  not not_9 (not_9_out, opcode_6_0);
  Comparator #(.width(2)) comparator_5 (
    .a(Instruction[13:12]), .b(2'b10), .gt(funct3_01_11), .eq(funct3_01_10));  // open: lt
  Comparator #(.width(2)) comparator_6 (
    .a(Instruction[13:12]), .b(2'b01), .eq(funct3_01_01), .lt(funct3_01_00));  // open: gt
  Comparator #(.width(1)) comparator_7 (.a(Instruction[14]), .b(1'b1), .eq(funct3_2_1), .lt(funct3_2_0));  // open: gt
  Comparator #(.width(2)) comparator_8 (
    .a(Instruction[26:25]), .b(2'b01), .eq(funct7_01_01), .lt(funct7_01_00));  // open: gt
  Comparator #(.width(2)) comparator_9 (
    .a(Instruction[30:29]), .b(2'b01), .eq(funct7_45_01), .lt(funct7_45_00));  // open: gt
  and and_36 (is_Btype, and_30_out, not_9_out);
  and and_37 (and_37_out, is_Rtype, funct3_01_10);
  and and_38 (and_38_out, is_Btype, funct3_01_11);
  and and_39 (and_39_out, is_Btype, funct3_01_10);
  and and_40 (is_mul, Rtype_funct3_000, funct7_01_01);
  and and_41 (is_or, and_37_out, funct3_2_1);
  not not_10 (not_10_out, funct3_2_1);
  and and_42 (is_srl, Rtype_funct3_101, funct7_45_00);
  and and_43 (is_bgeu, and_38_out, funct3_2_1);
  and and_44 (is_bltu, and_39_out, funct3_2_1);
  and and_45 (is_andi, is_Itype, funct3_01_11);
  and and_46 (and_46_out, opcode_23_01, opcode_45_10);
  not not_11 (not_11_out, funct7_01_01);
  and and_47 (is_srli, Itype_funct3_101, funct7_45_00);
  and and_48 (is_jalr, and_46_out, opcode_6_1);
  buf and_49 (Rtype_funct3_000_0, not_11_out);  // AND_Gate
  not not_12 (not_12_out, funct7_45_00);
  and and_50 (is_sw, is_Stype, funct3_01_10);
  and and_51 (is_lw, is_load, funct3_01_10);
  not not_13 (not_13_out, funct7_45_00);
  and and_52 (and_52_out, opcode_23_00, opcode_45_00);
  and and_53 (is_slt, and_37_out, not_10_out);
  buf and_54 (is_sra, not_12_out);  // AND_Gate
  buf and_55 (is_srai, not_13_out);  // AND_Gate
  and and_56 (is_load, and_52_out, opcode_6_0);
  not not_14 (not_14_out, BrEq);
  not not_15 (not_15_out, BrLt);
  and and_57 (and_57_out, is_beq, BrEq);
  and and_58 (and_58_out, is_bne, not_14_out);
  or or_1 (or_1_out, is_blt, is_bltu);
  or or_2 (or_2_out, is_bge, is_bgeu);
  and and_59 (and_59_out, or_1_out, BrLt);
  and and_60 (and_60_out, or_2_out, not_15_out);
  and and_61 (is_add, Rtype_funct3_000_0, funct7_45_00);
  or or_3 (or_3_out, and_57_out, and_58_out);
  or or_4 (or_4_out, and_59_out, and_60_out);
  and and_62 (and_62_out, opcode_23_00, opcode_45_01);
  not not_16 (not_16_out, funct7_45_00);
  and and_63 (is_sll, Rtype_funct3_001, funct7_01_00);
  or or_5 (or_5_out, is_jalr, is_jal);
  or or_6 (PCSel, or_5_out, or_7_out);
  or or_7 (or_7_out, or_3_out, or_4_out);
  and and_64 (is_Itype, and_62_out, opcode_6_0);
  buf and_65 (is_sub, not_16_out);  // AND_Gate
  not not_17 (not_17_out, funct7_01_00);
  buf and_66 (is_mulh, not_17_out);  // AND_Gate

  // Other names for the same wires on the sheet: opcode_01[1:0] = Instruction[1:0]; opcode_23[1:0] = Instruction[3:2];
  //   opcode_45[1:0] = Instruction[5:4]; opcode_6 = Instruction[6]; rd_imm[4:0] = Instruction[11:7];
  //   funct3_01[1:0] = Instruction[13:12]; funct3_2 = Instruction[14]; rs_imm[9:0] = Instruction[24:15];
  //   funct7_01[1:0] = Instruction[26:25]; funct7_23[1:0] = Instruction[28:27]; funct7_45[1:0] = Instruction[30:29];
  //   funct7_6 = Instruction[31]

  // Notes on the sheet:
  //   R TYPE
  //   S TYPE
  //   B TYPE
  //   LOAD TYPE
  //   I TYPE
  //   TYPES BY OPCODE
  //   INPUTS to your circuit
  //   INSTRUCTIONS BY OPCODE
  //   DON'T CHANGE THE LOCATIONS OF THE INPUTS AND OUTPUTS!
  //   Connect ROM Input here ->
  //   OUTPUT from your circuit
  //   contents of rom_1 (hex, n*v repeats v):
  //   102b 142b 162b 10ab 14ab 15ab 112b 122b 12ab 16ab 132b 13ab 61 61 61 1061 10e1 1161 1261 12e1 16e1
  //   1361 13e1 862 862 862 4*44 54 44 1047 17e7 2049 2061
  //   ROM FOR CONTROL LOGIC
  //   This is only if you choose to do the ROM option
  //   CONNECT
  //   WIRE
  //   TO
  //   USE
  //   ROM
  //   Reminder: If using ROM, use combinational logic for PCSel
endmodule
