// Logisim project imm-gen.circ as structural Verilog: 1 circuit, main circuit imm_gen
module imm_gen (
  input  [31:0] Instruction,
  input  [2:0] ImmSel,
  output [31:0] Immediate
);

  wire [31:0] ImmediateBtype, ImmediateItype;
  wire [31:11] ImmediateStype;
  wire [31:20] ImmediateJtype;

  Shifter #(.shift("ar"), .width(32)) shifter_1 (.in(Instruction), .\dist (5'b10100), .out(ImmediateItype));
  assign ImmediateStype = {{20{Instruction[31]}}, Instruction[31]};  // Bit_Extender bit_extender_1
  assign ImmediateBtype[31:12] = {{19{Instruction[31]}}, Instruction[31]};  // Bit_Extender bit_extender_2
  assign ImmediateJtype = {{11{Instruction[31]}}, Instruction[31]};  // Bit_Extender bit_extender_3
  Multiplexer #(.select(3), .width(32)) multiplexer_1 (
    .in0(ImmediateItype), .in1({ImmediateStype, Instruction[30:25], Instruction[11:7]}),
    .in2({ImmediateBtype[31:12], Instruction[7], Instruction[30:25], Instruction[11:8], ImmediateBtype[0]}),
    .in3({Instruction[31:12], {12{1'b0}}}),
    .in4({ImmediateJtype, Instruction[19:12], Instruction[20], Instruction[30:21], 1'b0}), .out(Immediate),
    .sel(ImmSel));  // open: in5, in6, in7

  // Other names for the same wires on the sheet: ImmediateBtype[11:1] = {Instruction[7], Instruction[30:25], Instruction[11:8]};
  //   ImmediateStype[10:0] = {Instruction[30:25], Instruction[11:7]};
  //   ImmediateJtype[19:1] = {Instruction[19:12], Instruction[20], Instruction[30:21]};
  //   ImmediateUtype[31:12] = Instruction[31:12]

  // Notes on the sheet:
  //   INPUTS to your circuit
  //   I types
  //   S types
  //   B types
  //   U types
  //   J types
  //   DON'T CHANGE THE LOCATIONS OF THE INPUTS AND OUTPUTS!
  //   OUTPUT from your circuit
endmodule
