// Logisim project partial-store.circ as structural Verilog: 1 circuit, main circuit partial_store
module partial_store (
  input  [31:0] Instruction,
  input  [31:0] MemAddress,
  input  [31:0] DataFromReg,
  input  MemWEn,
  output [3:0] MemWriteMask,
  output [31:0] DataToMem
);

  wire [3:0] ChangedMemWriteMask, StoreByteMask, StoreHalfByteMask;
  wire [31:0] ChangedDataToMem, StoreByte, StoreHalfByte;

  Multiplexer #(.select(2), .width(4)) multiplexer_1 (
    .in0(4'b0001), .in1(4'b0010), .in2(4'b0100), .in3(4'b1000), .out(StoreByteMask), .sel(MemAddress[1:0]));
  Multiplexer #(.select(2), .width(4)) multiplexer_2 (
    .in0(4'b0011), .in1(4'b1100), .out(StoreHalfByteMask), .sel(MemAddress[1:0]));  // open: in2, in3
  Multiplexer #(.select(3), .width(4)) multiplexer_3 (
    .in0(StoreByteMask), .in1(StoreHalfByteMask), .in2(4'b1111), .out(ChangedMemWriteMask),
    .sel(Instruction[14:12]));  // open: in3, in4, in5, in6, in7
  Multiplexer #(.width(4)) multiplexer_4 (
    .in0(4'b0000), .in1(ChangedMemWriteMask), .out(ChangedMemWriteMask), .sel(MemWEn));
  Multiplexer #(.select(2), .width(32)) multiplexer_5 (
    .in0({{24{1'b0}}, DataFromReg[7:0]}), .in1({{16{1'b0}}, DataFromReg[7:0], {8{1'b0}}}),
    .in2({{8{1'b0}}, DataFromReg[7:0], {16{1'b0}}}), .in3({DataFromReg[7:0], {24{1'b0}}}), .out(StoreByte),
    .sel(MemAddress[1:0]));
  Multiplexer #(.select(3), .width(32)) multiplexer_6 (
    .in0(StoreByte), .in1(StoreHalfByte), .in2(DataFromReg), .out(ChangedDataToMem), .sel(Instruction[14:12]));  // open: in3, in4, in5, in6, in7
  Multiplexer #(.width(32)) multiplexer_7 (.in0(DataFromReg), .in1(ChangedDataToMem), .out(DataToMem), .sel(MemWEn));
  Multiplexer #(.select(2), .width(32)) multiplexer_8 (
    .in0({{16{1'b0}}, DataFromReg[15:0]}), .in2({DataFromReg[15:0], {16{1'b0}}}), .out(StoreHalfByte),
    .sel(MemAddress[1:0]));  // open: in1, in3

  // Other names for the same wires on the sheet: BottomByte[7:0] = DataFromReg[7:0];
  //   BottomHalfByte[15:0] = DataFromReg[15:0]; StoreWord[31:0] = DataFromReg

  // Notes on the sheet:
  //   INPUTS to your circuit
  //   Store Byte Logic
  //   Write Mask Logic
  //   DON'T CHANGE THE LOCATIONS OF THE INPUTS AND OUTPUTS!
  //   Store Half Byte Logic
  //   OUTPUT from your circuit
endmodule
