// Logisim project regfile.circ as structural Verilog: 1 circuit, main circuit regfile
module regfile (
  input  [4:0] ReadIndex1,
  input  [4:0] ReadIndex2,
  input  [4:0] WriteIndex,
  input  [31:0] WriteData,
  input  RegWEn,
  input  clk,
  output [31:0] ra,
  output [31:0] sp,
  output [31:0] t0,
  output [31:0] t1,
  output [31:0] t2,
  output [31:0] s0,
  output [31:0] s1,
  output [31:0] a0,
  output [31:0] ReadData1,
  output [31:0] ReadData2
);

  wire a0r, a1r, a2r, a3r, a4r, a5r, a6r, a7r, gpr, rar, s0r, s1r, s2r, s3r, s4r, s5r, s6r, s7r, s8r, s9r,
       s10r, s11r, spr, t0r, t1r, t2r, t3r, t4r, t5r, t6r, tpr, x0r;
  wire [31:0] a0i, a1, a1i, a2, a2i, a3, a3i, a4, a4i, a5, a5i, a6, a6i, a7, a7i, gp, gpi, rai, s0i, s1i, s2,
       s2i, s3, s3i, s4, s4i, s5, s5i, s6, s6i, s7, s7i, s8, s8i, s9, s9i, s10, s10i, s11, s11i, spi, t0i,
       t1i, t2i, t3, t3i, t4, t4i, t5, t5i, t6, t6i, tp, tpi, x0i;

  Register #(.width(32)) x0 (.D(x0i), .en(x0r), .clk(clk), .clr(1'b0));  // open: Q
  Register #(.width(32)) register_1 (.D(rai), .en(rar), .clk(clk), .Q(ra), .clr(1'b0));
  Register #(.width(32)) register_2 (.D(spi), .en(spr), .clk(clk), .Q(sp), .clr(1'b0));
  Register #(.width(32)) register_3 (.D(gpi), .en(gpr), .clk(clk), .Q(gp), .clr(1'b0));
  Register #(.width(32)) register_4 (.D(t0i), .en(t0r), .clk(clk), .Q(t0), .clr(1'b0));
  Register #(.width(32)) register_5 (.D(t1i), .en(t1r), .clk(clk), .Q(t1), .clr(1'b0));
  Register #(.width(32)) register_6 (.D(t2i), .en(t2r), .clk(clk), .Q(t2), .clr(1'b0));
  Register #(.width(32)) register_7 (.D(s0i), .en(s0r), .clk(clk), .Q(s0), .clr(1'b0));
  Register #(.width(32)) register_8 (.D(s1i), .en(s1r), .clk(clk), .Q(s1), .clr(1'b0));
  Register #(.width(32)) register_9 (.D(a0i), .en(a0r), .clk(clk), .Q(a0), .clr(1'b0));
  Register #(.width(32)) register_10 (.D(a1i), .en(a1r), .clk(clk), .Q(a1), .clr(1'b0));
  Register #(.width(32)) register_11 (.D(a2i), .en(a2r), .clk(clk), .Q(a2), .clr(1'b0));
  Register #(.width(32)) register_12 (.D(a3i), .en(a3r), .clk(clk), .Q(a3), .clr(1'b0));
  Register #(.width(32)) register_13 (.D(a4i), .en(a4r), .clk(clk), .Q(a4), .clr(1'b0));
  Register #(.width(32)) register_14 (.D(a5i), .en(a5r), .clk(clk), .Q(a5), .clr(1'b0));
  Register #(.width(32)) register_15 (.D(a6i), .en(a6r), .clk(clk), .Q(a6), .clr(1'b0));
  Register #(.width(32)) register_16 (.D(a7i), .en(a7r), .clk(clk), .Q(a7), .clr(1'b0));
  Register #(.width(32)) register_17 (.D(s2i), .en(s2r), .clk(clk), .Q(s2), .clr(1'b0));
  Register #(.width(32)) register_18 (.D(s3i), .en(s3r), .clk(clk), .Q(s3), .clr(1'b0));
  Register #(.width(32)) register_19 (.D(s4i), .en(s4r), .clk(clk), .Q(s4), .clr(1'b0));
  Register #(.width(32)) register_20 (.D(s5i), .en(s5r), .clk(clk), .Q(s5), .clr(1'b0));
  Register #(.width(32)) register_21 (.D(s6i), .en(s6r), .clk(clk), .Q(s6), .clr(1'b0));
  Register #(.width(32)) register_22 (.D(s7i), .en(s7r), .clk(clk), .Q(s7), .clr(1'b0));
  Register #(.width(32)) register_23 (.D(s8i), .en(s8r), .clk(clk), .Q(s8), .clr(1'b0));
  Register #(.width(32)) register_24 (.D(s9i), .en(s9r), .clk(clk), .Q(s9), .clr(1'b0));
  Register #(.width(32)) register_25 (.D(s10i), .en(s10r), .clk(clk), .Q(s10), .clr(1'b0));
  Register #(.width(32)) register_26 (.D(s11i), .en(s11r), .clk(clk), .Q(s11), .clr(1'b0));
  Register #(.width(32)) register_27 (.D(t3i), .en(t3r), .clk(clk), .Q(t3), .clr(1'b0));
  Register #(.width(32)) register_28 (.D(t4i), .en(t4r), .clk(clk), .Q(t4), .clr(1'b0));
  Register #(.width(32)) register_29 (.D(t5i), .en(t5r), .clk(clk), .Q(t5), .clr(1'b0));
  Register #(.width(32)) register_30 (.D(t6i), .en(t6r), .clk(clk), .Q(t6), .clr(1'b0));
  Register #(.width(32)) register_31 (.D(tpi), .en(tpr), .clk(clk), .Q(tp), .clr(1'b0));
  Demultiplexer #(.select(5)) demultiplexer_1 (
    .out0(x0r), .out1(rar), .out2(spr), .out3(gpr), .out4(tpr), .out5(t0r), .out6(t1r), .out7(t2r),
    .out8(s0r), .out9(s1r), .out10(a0r), .out11(a1r), .out12(a2r), .out13(a3r), .out14(a4r), .out15(a5r),
    .out16(a6r), .out17(a7r), .out18(s2r), .out19(s3r), .out20(s4r), .out21(s5r), .out22(s6r), .out23(s7r),
    .out24(s8r), .out25(s9r), .out26(s10r), .out27(s11r), .out28(t3r), .out29(t4r), .out30(t5r), .out31(t6r),
    .in(RegWEn), .sel(WriteIndex));
  Demultiplexer #(.select(5), .width(32)) demultiplexer_2 (
    .out0(x0i), .out1(rai), .out2(spi), .out3(gpi), .out4(tpi), .out5(t0i), .out6(t1i), .out7(t2i),
    .out8(s0i), .out9(s1i), .out10(a0i), .out11(a1i), .out12(a2i), .out13(a3i), .out14(a4i), .out15(a5i),
    .out16(a6i), .out17(a7i), .out18(s2i), .out19(s3i), .out20(s4i), .out21(s5i), .out22(s6i), .out23(s7i),
    .out24(s8i), .out25(s9i), .out26(s10i), .out27(s11i), .out28(t3i), .out29(t4i), .out30(t5i), .out31(t6i),
    .in(WriteData), .sel(WriteIndex));
  Multiplexer #(.select(5), .width(32)) multiplexer_1 (
    .in0({32{1'b0}}), .in1(ra), .in2(sp), .in3(gp), .in4(tp), .in5(t0), .in6(t1), .in7(t2), .in8(s0),
    .in9(s1), .in10(a0), .in11(a1), .in12(a2), .in13(a3), .in14(a4), .in15(a5), .in16(a6), .in17(a7),
    .in18(s2), .in19(s3), .in20(s4), .in21(s5), .in22(s6), .in23(s7), .in24(s8), .in25(s9), .in26(s10),
    .in27(s11), .in28(t3), .in29(t4), .in30(t5), .in31(t6), .out(ReadData1), .sel(ReadIndex1));
  Multiplexer #(.select(5), .width(32)) multiplexer_2 (
    .in0({32{1'b0}}), .in1(ra), .in2(sp), .in3(gp), .in4(tp), .in5(t0), .in6(t1), .in7(t2), .in8(s0),
    .in9(s1), .in10(a0), .in11(a1), .in12(a2), .in13(a3), .in14(a4), .in15(a5), .in16(a6), .in17(a7),
    .in18(s2), .in19(s3), .in20(s4), .in21(s5), .in22(s6), .in23(s7), .in24(s8), .in25(s9), .in26(s10),
    .in27(s11), .in28(t3), .in29(t4), .in30(t5), .in31(t6), .out(ReadData2), .sel(ReadIndex2));

  // Notes on the sheet:
  //   INPUTS to your circuit
  //   DON'T CHANGE THE LOCATIONS OF THE INPUTS AND OUTPUTS!
  //   These are DEBUG/TEST outputs from your circuit.
  //   OUTPUTS from your circuit
endmodule
